# Fritzing sketch pb circuit (saved by Fritzing 0.9.3b)
breadboards: 2

parts:
  Part1 = Adafruit OLED FeatherWing [part_number="Adafruit #2900"]
  Part2 = Adafruit Feather M0 Express [part_number="Adafruit #3403"]
  ENCODER1 = Rotary Encoder with Knob
  U1 = LM124-324 Quad Opamp [package="DIP (Dual Inline)"]
  R6 = Resistor [tolerance=±5% resistance=1k package=THT]
  R7 = Resistor [tolerance=±5% resistance=39k package=THT]
  R8 = Resistor [tolerance=±5% resistance=56k package=THT]
  Ubeat = 3.5mm Audio Jack [package=audio-jack-3.5mm-smd]
  R10 = Resistor [tolerance=±5% resistance=1k package=THT]
  R11 = Resistor [tolerance=±5% resistance=39k package=THT]
  R12 = Resistor [tolerance=±5% resistance=56k package=THT]
  Utuplet = 3.5mm Audio Jack [package=audio-jack-3.5mm-smd]
  R14 = Resistor [tolerance=±5% resistance=1k package=THT]
  R15 = Resistor [tolerance=±5% resistance=39k package=THT]
  R16 = Resistor [tolerance=±5% resistance=56k package=THT]
  Useq = 3.5mm Audio Jack [package=audio-jack-3.5mm-smd]
  R18 = Resistor [tolerance=±5% resistance=1k package=THT]
  R19 = Resistor [tolerance=±5% resistance=39k package=THT]
  R20 = Resistor [tolerance=±5% resistance=56k package=THT]
  Umeas = 3.5mm Audio Jack [package=audio-jack-3.5mm-smd]
  Lmeas = LED - 5mm [color="Red (633nm)" package="5 mm [THT]"]
  Lseq = LED - 5mm [color="Red (633nm)" package="5 mm [THT]"]
  R21 = Resistor [tolerance=±5% resistance=10k package=THT]
  R22 = Resistor [tolerance=±5% resistance=10k package=THT]
  Lbeat = LED - 5mm [color="Green (565nm)" package="5 mm [THT]"]
  R23 = Resistor [tolerance=±5% resistance=1k package=THT]
  Ltuplet = LED - 5mm [color="Green (565nm)" package="5 mm [THT]"]
  R24 = Resistor [tolerance=±5% resistance=1k package=THT]
  R25 = Resistor [tolerance=±5% resistance=100k package=THT]
  Q1 = NPN-Transistor [package="TO92 [THT]"]
  R27 = Resistor [tolerance=±5% resistance=100k package=THT]
  D1 = Rectifier Diode [part_number=1N4001 package="300 mil [THT]"]
  Jclkin = BANANA_CONN [package=banana_conn]
  R28 = Resistor [tolerance=±5% resistance=100k package=THT]
  Q2 = NPN-Transistor [package="TO92 [THT]"]
  R30 = Resistor [tolerance=±5% resistance=100k package=THT]
  D2 = Rectifier Diode [part_number=1N4001 package="300 mil [THT]"]
  Jother = BANANA_CONN [package=banana_conn]

nets:
  GND: Part1.GND, Part2.GND, ENCODER1.no_name_yet#2, ENCODER1.no_name_yet#5, U1.VCC-, R7.Pin_0, Ubeat.SLEEVE, R11.Pin_1, Utuplet.SLEEVE, R15.Pin_0, Useq.SLEEVE, R19.Pin_1, Umeas.SLEEVE, R21.Pin_1, R22.Pin_0, R23.Pin_0, R24.Pin_1, Q1.E, R27.Pin_0, D1.anode, Q2.E, R30.Pin_0, D2.anode
  3.3V: Part1.3.3V, Part2.+3V3, U1.VCC+
  N1: Part1.!RESET, Part2.!RESET
  N2: Part1.SDA, Part2.SDA
  N3: Part1.SCL, Part2.SCL
  N4: Part1.H, Part2.D5
  N5: Part1.I, Part2.D6
  N6: Part1.J, Part2.D9
  Tseq: Part2.TX, U1.2IN+, Lseq.anode
  Tbeat: Part2.MISO, U1.1IN+, Lbeat.anode
  Tmeas: Part2.MOSI, U1.3IN+, Lmeas.anode
  Ttuplet: Part2.SCK, U1.4IN+, Ltuplet.anode
  Tother: Part2.A2, Q2.C
  Tclkin: Part2.A1, Q1.C
  N7: Part2.D12, ENCODER1.no_name_yet#3
  N8: Part2.D11, ENCODER1.no_name_yet#1
  N9: Part2.D10, ENCODER1.no_name_yet#4
  N10: U1.1OUT, R6.Pin_0, R8.Pin_1
  N11: U1.1IN-, R7.Pin_1, R8.Pin_0
  N12: U1.2IN-, R15.Pin_1, R16.Pin_0
  N13: U1.2OUT, R14.Pin_0, R16.Pin_1
  N14: U1.3OUT, R18.Pin_0, R20.Pin_0
  N15: U1.3IN-, R19.Pin_0, R20.Pin_1
  N16: U1.4IN-, R11.Pin_0, R12.Pin_1
  N17: U1.4OUT, R10.Pin_0, R12.Pin_0
  N18: R6.Pin_1, Ubeat.RIGHT
  N19: R10.Pin_1, Utuplet.RIGHT
  N20: R14.Pin_1, Useq.RIGHT
  N21: R18.Pin_1, Umeas.RIGHT
  N22: Lmeas.cathode, R21.Pin_0
  N23: Lseq.cathode, R22.Pin_1
  N24: Lbeat.cathode, R23.Pin_1
  N25: Ltuplet.cathode, R24.Pin_0
  N26: R25.Pin_0, Jclkin.1
  N27: R25.Pin_1, Q1.B, R27.Pin_1, D1.cathode
  N28: R28.Pin_0, Jother.1
  N29: R28.Pin_1, Q2.B, R30.Pin_1, D2.cathode

custom parts:
  Adafruit OLED FeatherWing: This is the FeatherWing OLED: it adds a 128x32 monochrome OLED plus 3 user buttons to any Feather main board. These displays are small, only about 1" diagonal, but very readable due to the high contrast of an OLED display. This screen is made of 128x32 individual white OLED pixels and because the display makes its own light, no backlight is required. This reduces the power required to run the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
  Adafruit Feather M0 Express: We love all our Feathers equally, but this Feather is very special. It's our first Feather that is specifically designed for use with CircuitPython! CircuitPython is our beginner-oriented flavor of MicroPython - and as the name hints at, its a small but full-featured version of the popular Python programming language specifically for use with circuitry and electronics. That doesn't mean you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
  Rotary Encoder with Knob: Rotary Encoder with 1/4" Shaft and Knob
